# Fritzing sketch Arduino Day (saved by Fritzing 0.9.2b)
breadboards: 1

parts:
  R1 = Resistor [tolerance=±5% resistance=220 package=THT]
  R2 = Resistor [tolerance=±5% resistance=220 package=THT]
  R3 = Resistor [tolerance=±5% resistance=220 package=THT]
  RE1 = Rotary Encoder [package=THT]
  Part1 = Arduino Uno (Rev3)
  S1 = Pushbutton [package="[THT]"]
  S2 = Pushbutton [package="[THT]"]
  LED1 = smd LED [color="Red (633nm)" package="0805 [SMD]"]

nets:
  N1: R1.Pin_0, R2.Pin_0, R3.Pin_0, RE1.EncoderPinA, Part1.GND
  N2: R1.Pin_1, Part1.D4, S2.Pin_3, S2.Pin_4
  N3: R2.Pin_1, Part1.D7, S1.Pin_3, S1.Pin_4
  N4: R3.Pin_1, LED1.anode
  N5: RE1.EncoderPinC, Part1.A0
  N6: RE1.EncoderPinB, Part1.5V, S1.Pin_1, S1.Pin_2, S2.Pin_1, S2.Pin_2
  N7: Part1.D13/SCK, LED1.cathode
